# Fritzing sketch breadboard (saved by Fritzing 0.9.3b)
breadboards: 1

parts:
  Part1 = Arduino Mega ADK (Rev3)
  U1 = RF-LINK_TX [package=rf-link_tx]
  Part2 = blueIOT core
  U2 = RF-LINK_RX [package=rf-link_rx]

nets:
  N1: Part1.D19/RX1, Part2.TXD
  N2: Part1.D18/TX1, Part2.RXD
  3V3: Part1.3V3, Part2.VCC
  GND: Part1.GND, U1.GND, Part2.GND, U2.GND
  N3: Part1.D3_PWM, U1.DATA
  N4: Part1.D5_PWM, U2.DATA
  +5V: U1.+5V, U2.+5V
